# Fritzing sketch eclairage_voiture (saved by Fritzing 0.9.6b)

parts:
  Composant1 = Arduino Nano (Rev3.0)
  LED1 = LED - 3mm [color="Red (633nm)" current=0.030 package="3 mm [THT]"]
  LED2 = LED - 3mm [color="Red (633nm)" current=0.030 package="3 mm [THT]"]
  LED3 = LED - 3mm [color="White (6500K)" current=0.030 package="3 mm [THT]"]
  LED4 = LED - 3mm [color="White (6500K)" current=0.030 package="3 mm [THT]"]
  LED5 = LED - 3mm [color="Orange (612nm)" current=0.030 package="3 mm [THT]"]
  LED6 = LED - 3mm [color="Orange (612nm)" current=0.030 package="3 mm [THT]"]
  LED7 = LED - 3mm [color="Orange (612nm)" current=0.030 package="3 mm [THT]"]
  LED8 = LED - 3mm [color="Orange (612nm)" current=0.030 package="3 mm [THT]"]
  R2 = Resistor [tolerance=±5% resistance=3.7k power=0.25 package=THT]
  R4 = Resistor [tolerance=±5% resistance=3.7k power=0.25 package=THT]
  R5 = Resistor [tolerance=±5% resistance=3.7k power=0.25 package=THT]
  R6 = Resistor [tolerance=±5% resistance=3.7k power=0.25 package=THT]
  R7 = Resistor [tolerance=±5% resistance=3.7k power=0.25 package=THT]
  R8 = Resistor [tolerance=±5% resistance=3.7k power=0.25 package=THT]
  R1 = Resistor [tolerance=±5% resistance=3.7k power=0.25 package=THT]
  R9 = Resistor [tolerance=±5% resistance=3.7k package="0402 [SMD]"]
  Feux_de_nuit = Arduino Nano (Rev3.0)  # not connected
  Nuit_et_frainage = Arduino Nano (Rev3.0)
  Nuit_freinage_appel_de_phares = Arduino Nano (Rev3.0)
  Stationnement_à_droite_la_nuit = Arduino Nano (Rev3.0)
  Stationnement_à_droite_le_jour = Arduino Nano (Rev3.0)
  Stationnement_droite_+_détresse = Arduino Nano (Rev3.0)
  Nuit_et_feux_de_détresse = Arduino Nano (Rev3.0)
  Tourner_à_droite_la_nuit = Arduino Nano (Rev3.0)

nets:
  N1: Composant1.GND, Composant1.D6, Composant1.D7, Composant1.D8, LED1.anode, LED2.anode, LED3.anode, LED4.anode, LED5.anode, LED6.anode, LED7.anode, LED8.anode
  N2: Composant1.D2, R7.Pin_0, R9.Pin_0
  N3: Composant1.D3, R2.Pin_0, R1.Pin_0
  N4: Composant1.D4, R4.Pin_0, R8.Pin_0
  N5: Composant1.D5, R5.Pin_0, R6.Pin_0
  N6: Nuit_et_frainage.D6, Nuit_et_frainage.GND
  N7: Nuit_freinage_appel_de_phares.D7, Nuit_freinage_appel_de_phares.GND
  N8: Stationnement_à_droite_la_nuit.D6, Stationnement_à_droite_la_nuit.D7, Stationnement_à_droite_la_nuit.GND
  N9: Stationnement_à_droite_le_jour.D6, Stationnement_à_droite_le_jour.D7, Stationnement_à_droite_le_jour.D8, Stationnement_à_droite_le_jour.GND
  N10: Stationnement_droite_+_détresse.D6, Stationnement_droite_+_détresse.GND
  N11: Nuit_et_feux_de_détresse.D8, Nuit_et_feux_de_détresse.GND
  N12: Tourner_à_droite_la_nuit.GND, Tourner_à_droite_la_nuit.D7, Tourner_à_droite_la_nuit.D8
